# Fritzing sketch ThreeScan (saved by Fritzing 0.9.3b)
breadboards: 1

parts:
  U1 = ESP32S-HiLetgo [part_number=ESP32S-HiLetgo]
  J1 = Basic Servo
  microSD1 = MicroSD Card Module
  C1 = Electrolytic Capacitor [capacitance=1µF package="100 mil [THT, electrolytic]"]
  U2 = LIPO-1000mAh [package=lipo-1000]
  U3 = Hirose DF13 Series Header [part_number=DF13#-6P-1.25V package=DF13C-6P-1.25V]

nets:
  N1: U1.3.3, microSD1.VCC
  N2: U1.GPIO26, U3.4
  N3: U1.GPIO27, U3.5
  GND: U1.GND, J1.gnd, microSD1.GND, C1.-, U2.-, U3.1
  VIN: U1.VIN, J1.vcc, C1.+, U2.+, U3.6
  N4: U1.GPIO4, J1.pulse
  N5: U1.GPIO5, microSD1.CS
  N6: U1.GPIO18, microSD1.SCK
  N7: U1.GPIO19, microSD1.MISO
  N8: U1.GPIO23, microSD1.MOSI

notes:
  RX
  TX

custom parts:
  ESP32S-HiLetgo: HiLetgo ESP-WROOM-32 ESP32 ESP-32S Development Board 2.4GHz Dual-Mode WiFi + Bluetooth Dual Cores Microcontroller The ESP32 integrated with Antenna switches, RF Balun, power amplifiers, low-noise amplifiers, filters, and management modules, and the entire solution occupies the least area of PCB. 2.4 GHz Wi-Fi plus Bluetooth dual-mode chip, with TSMC Ultra-low power consumption 40nm technology,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
